// Logisim project Alu.circ as structural Verilog: 7 circuits, main circuit main
module main (
  input  cin,
  input  A,
  input  B,
  input  Bin,
  input  [3:0] opcode,
  output out_6,
  output out_7
);

  wire adder_1_out, and_1_out, comparator_1_lt, multiplexer_1_out, not_1_out, not_2_out, not_3_out, or_1_out,
       shifter_1_out;

  not not_1 (not_1_out, B);
  Multiplexer multiplexer_1 (.in0(not_1_out), .in1(B), .out(multiplexer_1_out), .sel(Bin));  // open: en
  Adder #(.width(1)) adder_1 (.a(A), .b(multiplexer_1_out), .out(adder_1_out), .cin(cin), .cout(out_7));
  Shifter #(.width(1)) shifter_1 (.in(A), .\dist (multiplexer_1_out), .out(shifter_1_out));
  Comparator #(.width(1)) comparator_1 (.a(multiplexer_1_out), .b(A), .lt(comparator_1_lt));  // open: gt, eq
  and and_1 (and_1_out, A, multiplexer_1_out);
  or or_1 (or_1_out, A, multiplexer_1_out);
  not not_2 (not_2_out, and_1_out);
  not not_3 (not_3_out, or_1_out);
  Multiplexer #(.select(4)) multiplexer_2 (
    .in0(adder_1_out), .in1(adder_1_out), .in2(adder_1_out), .in3(adder_1_out), .in4(adder_1_out),
    .in5(shifter_1_out), .in6(adder_1_out), .in8(and_1_out), .in9(not_3_out), .in10(not_2_out),
    .in11(comparator_1_lt), .in12(comparator_1_lt), .in14(adder_1_out), .in15(adder_1_out), .out(out_6),
    .sel(opcode));  // open: in7, in13, en
endmodule

module _4_bit_alu (
  input  in_1,
  input  [3:0] in_2,
  input  [3:0] in_3,
  input  in_4,
  input  [7:0] in_5,
  input  [3:0] in_6,
  input  [7:0] in_7,
  input  in_8,
  input  in_9,
  output [3:0] out_10,
  output out_11,
  output [7:0] out_12
);

  wire main_1_out_7, main_2_out_7, main_3_out_7;
  wire [7:0] register_1_q, subtractor_1_out;

  main main_1 (
    .cin(in_1), .A(in_2[0]), .B(in_3[0]), .Bin(in_4), .opcode(in_6), .out_6(out_10[0]), .out_7(main_1_out_7));
  main main_2 (
    .cin(main_1_out_7), .A(in_2[1]), .B(in_3[1]), .Bin(in_4), .opcode(in_6), .out_6(out_10[1]),
    .out_7(main_2_out_7));
  main main_3 (
    .cin(main_2_out_7), .A(in_2[2]), .B(in_3[2]), .Bin(in_4), .opcode(in_6), .out_6(out_10[2]),
    .out_7(main_3_out_7));
  main main_4 (
    .cin(main_3_out_7), .A(in_2[3]), .B(in_3[3]), .Bin(in_4), .opcode(in_6), .out_6(out_10[3]), .out_7(out_11));
  Register register_1 (.D(out_12), .Q(register_1_q), .clk(in_8));  // open: en, clr
  Subtractor subtractor_1 (.a(in_5), .b(in_7), .out(subtractor_1_out));  // open: bin, bout
  ROM rom_1 (.addr(register_1_q));  // open: data, sel
  Multiplexer #(.width(8)) multiplexer_1 (.in0(in_5), .in1(subtractor_1_out), .out(out_12), .sel(in_9));  // open: en

  // Notes on the sheet:
  //   contents of rom_1 (hex, n*v repeats v):
  //   55 55 5 5 55 55 5 25 1 55 55 5
endmodule

module _8_bit_alu (
  input  in_1,
  input  [7:0] in_2,
  input  [7:0] in_3,
  input  in_4,
  input  [3:0] in_5,
  output [7:0] out_6,
  output out_7
);

  wire n4_bit_alu_1_out_11;

  _4_bit_alu u_4_bit_alu_1 (
    .in_1(in_1), .in_2(in_2[3:0]), .in_3(in_3[3:0]), .in_4(in_4), .in_6(in_5), .out_10(out_6[3:0]),
    .out_11(n4_bit_alu_1_out_11));  // open: in_8, in_9, in_5, in_7, out_12
  _4_bit_alu u_4_bit_alu_2 (
    .in_1(n4_bit_alu_1_out_11), .in_2(in_2[7:4]), .in_3(in_3[7:4]), .in_4(in_4), .in_6(in_5),
    .out_10(out_6[7:4]), .out_11(out_7));  // open: in_8, in_9, in_5, in_7, out_12
endmodule

module full_8_bit_alu (
  input  cin,
  input  [7:0] in_2,
  input  [7:0] in_3,
  input  Bin,
  input  [3:0] opcode,
  output [7:0] out_6,
  output out_7,
  output [7:0] out_8
);

  wire comparator_1_lt;
  wire [2:0] bit_extender_1_out;
  wire [7:0] adder_1_out, and_1_out, bit_extender_2_out, multiplexer_1_out, not_1_out, not_2_out, or_2_out,
       shifter_1_out, undriven;

  assign not_1_out = ~in_3;  // NOT_Gate not_1, 8 bits wide
  Multiplexer #(.width(8)) multiplexer_1 (.in0(not_1_out), .in1(in_3), .out(multiplexer_1_out), .sel(Bin));  // open: en
  Bit_Extender #(.out_width(3)) bit_extender_1 (.in(multiplexer_1_out), .out(bit_extender_1_out));
  Adder adder_1 (.a(in_2), .b(multiplexer_1_out), .out(adder_1_out), .cin(cin), .cout(out_7));
  Shifter shifter_1 (.in(in_2), .\dist (bit_extender_1_out), .out(shifter_1_out));
  Comparator comparator_1 (.a(multiplexer_1_out), .b(in_2), .lt(comparator_1_lt));  // open: gt, eq
  assign and_1_out = in_2 & multiplexer_1_out;  // AND_Gate and_1, 8 bits wide
  // OR_Gate or_1 has open pins: in0=in_2, in1=multiplexer_1_out, out=open
  assign not_2_out = ~and_1_out;  // NOT_Gate not_2, 8 bits wide
  assign bit_extender_2_out = {{7{1'b0}}, comparator_1_lt};  // Bit_Extender bit_extender_2
  assign or_2_out = adder_1_out | {8{1'b0}};  // OR_Gate or_2, 8 bits wide
  Multiplexer #(.select(4), .width(8)) multiplexer_2 (
    .in0(adder_1_out), .in1(adder_1_out), .in2(adder_1_out), .in3(adder_1_out), .in4(adder_1_out),
    .in5(shifter_1_out), .in6(adder_1_out), .in7(multiplexer_1_out), .in8(and_1_out),
    .in9(multiplexer_1_out), .in10(not_2_out), .in11(bit_extender_2_out), .in12(undriven), .in13(in_2),
    .in14(in_2), .in15(multiplexer_1_out), .out(out_6), .sel(opcode));  // open: en
  assign out_8 = ~or_2_out;  // NOT_Gate not_3, 8 bits wide

  // Notes on the sheet:
  //   A
  //   B
endmodule

module circuit (
  input  in_1,
  input  [7:0] in_2,
  input  [7:0] in_3,
  input  in_4,
  input  [3:0] in_5,
  output [7:0] out_6,
  output out_7,
  output [7:0] out_8
);

  // full_8_bit_alu full_8_bit_alu_1: pin names not known; wires that end beside it: in_1, in_2, in_3, in_4, in_5, out_6, out_7, out_8
endmodule

module _8_bit_register_file (
  input  [1:0] Read_Register_Number_1,
  input  [1:0] Write_Register,
  input  [1:0] Read_Register_Number_2,
  input  [7:0] Write_Data,
  input  in_5,
  input  in_6,
  output [7:0] Read_Data_1,
  output [7:0] Read_Data_2
);

  wire decoder_1_out0, decoder_1_out1, decoder_1_out2, decoder_1_out3;
  wire [7:0] Register_0_q, Register_1_q, Register_2_q, Register_3_q;

  Decoder #(.select(2)) decoder_1 (
    .out0(decoder_1_out0), .out1(decoder_1_out1), .out2(decoder_1_out2), .out3(decoder_1_out3),
    .sel(Write_Register));  // open: en
  Register Register_0 (.D(Write_Data), .en(decoder_1_out0), .Q(Register_0_q), .clk(in_5), .clr(in_6));
  Register Register_1 (.D(Write_Data), .en(decoder_1_out1), .Q(Register_1_q), .clk(in_5), .clr(in_6));
  Register Register_2 (.D(Write_Data), .en(decoder_1_out2), .Q(Register_2_q), .clk(in_5), .clr(in_6));
  Register Register_3 (.D(Write_Data), .en(decoder_1_out3), .Q(Register_3_q), .clk(in_5), .clr(in_6));
  Multiplexer #(.select(2), .width(8)) multiplexer_1 (
    .in0(Register_0_q), .in1(Register_1_q), .in2(Register_2_q), .in3(Register_3_q), .out(Read_Data_1),
    .sel(Read_Register_Number_1));  // open: en
  Multiplexer #(.select(2), .width(8)) multiplexer_2 (
    .in0(Register_0_q), .in1(Register_1_q), .in2(Register_2_q), .in3(Register_3_q), .out(Read_Data_2),
    .sel(Read_Register_Number_2));  // open: en
endmodule

module Data_path (
  input  CLR,
  output [7:0] out_2,
  output [7:0] out_3,
  output [7:0] out_4,
  output [7:0] out_5,
  output [7:0] out_6,
  output [7:0] out_7,
  output [7:0] out_8,
  output [1:0] out_9,
  output [2:0] out_10,
  output [1:0] out_11,
  output [7:0] out_12,
  output [1:0] out_13,
  output [7:0] out_14,
  output [1:0] r2,
  output [7:0] out_16,
  output [7:0] out_17,
  output [7:0] out_18,
  output out_19,
  output [7:0] out_20,
  output [3:0] out_21,
  output [7:0] out_22,
  output [7:0] out_23
);

  wire and_1_out, button_1_out, button_2_out, clock_1_out, comparator_1_eq, decoder_1_out0, decoder_1_out1,
       decoder_1_out2, decoder_1_out3, decoder_1_out4, decoder_1_out5, decoder_1_out6, decoder_1_out7,
       decoder_1_out8, decoder_1_out9, decoder_1_out10, decoder_1_out11, decoder_1_out12, decoder_1_out13,
       decoder_1_out14, decoder_1_out15, or_1_out, or_2_out, or_3_out, or_4_out, or_5_out, or_6_out,
       undriven, xor_1_out;
  wire [1:0] multiplexer_2_out, rom_1_data;
  wire [7:0] adder_2_out, bit_extender_1_out, bit_extender_2_out, bit_extender_3_out, ram_1_data,
       register_1_q;

  or or_1 (or_1_out, decoder_1_out5, decoder_1_out4, decoder_1_out3);
  Clock clock_1 (.out(clock_1_out));
  Button button_1 (.out(button_1_out));
  Button button_2 (.out(button_2_out));
  assign bit_extender_1_out = {{7{1'b0}}, 1'b1};  // Bit_Extender bit_extender_1
  or or_2 (or_2_out, decoder_1_out11, decoder_1_out13, decoder_1_out12, decoder_1_out14);
  Register register_1 (.D(out_4), .Q(register_1_q), .clk(clock_1_out), .clr(button_1_out));  // open: en
  Adder adder_1 (.a(register_1_q), .b(bit_extender_1_out), .out(out_3));  // open: cin, cout
  or or_3 (or_3_out, decoder_1_out2, decoder_1_out6);
  Multiplexer #(.width(2)) multiplexer_1 (
    .in0(multiplexer_2_out), .in1(out_13), .out(r2), .sel(decoder_1_out4));  // open: en
  Decoder #(.select(4)) decoder_1 (
    .out0(decoder_1_out0), .out1(decoder_1_out1), .out2(decoder_1_out2), .out3(decoder_1_out3),
    .out4(decoder_1_out4), .out5(decoder_1_out5), .out6(decoder_1_out6), .out7(decoder_1_out7),
    .out8(decoder_1_out8), .out9(decoder_1_out9), .out10(decoder_1_out10), .out11(decoder_1_out11),
    .out12(decoder_1_out12), .out13(decoder_1_out13), .out14(decoder_1_out14), .out15(decoder_1_out15),
    .sel(out_21));  // open: en
  xor xor_1 (xor_1_out, or_3_out, 1'b1);
  Multiplexer #(.width(2)) multiplexer_2 (
    .in0(rom_1_data), .in1(2'b00), .out(multiplexer_2_out), .sel(decoder_1_out6));  // open: en
  ROM rom_1 (.addr(register_1_q), .data({out_21, out_13, rom_1_data}));  // open: sel
  Multiplexer #(.width(2)) multiplexer_3 (.in0(out_13), .in1(2'b00), .out(out_9), .sel(or_2_out));  // open: en
  Multiplexer #(.width(2)) multiplexer_4 (.in0(out_13), .in1(2'b00), .out(out_11), .sel(or_1_out));  // open: en
  assign bit_extender_2_out = {{6{1'b0}}, rom_1_data};  // Bit_Extender bit_extender_2
  assign bit_extender_3_out = {{7{1'b0}}, 1'b1};  // Bit_Extender bit_extender_3
  _8_bit_register_file u_8_bit_register_file_1 (
    .Write_Data(out_8), .Read_Data_1(out_17), .Read_Data_2(out_16), .Write_Register(out_9),
    .Read_Register_Number_1(out_11), .Read_Register_Number_2(r2), .in_5(clock_1_out), .in_6(button_2_out));
  Bit_Extender #(.out_width(3)) bit_extender_4 (.in(bit_extender_2_out), .out(out_10));
  Multiplexer #(.width(8)) multiplexer_5 (
    .in0(out_16), .in1(bit_extender_2_out), .out(out_18), .sel(or_4_out));  // open: en
  Shifter shifter_1 (.in(bit_extender_3_out), .\dist (out_10), .out(out_2));
  or or_4 (or_4_out, decoder_1_out15, decoder_1_out1, decoder_1_out3, decoder_1_out5, decoder_1_out12, decoder_1_out4);
  Subtractor subtractor_1 (.a(out_3), .b(out_2), .out(out_5));  // open: bin, bout
  Adder adder_2 (.a(out_3), .b(out_2), .out(adder_2_out));  // open: cin, cout
  Multiplexer #(.width(8)) multiplexer_6 (.in0(out_6), .in1(out_5), .out(out_4), .sel(decoder_1_out9), .en(undriven));
  Multiplexer #(.width(8)) multiplexer_7 (.in0(out_3), .in1(adder_2_out), .out(out_6), .sel(or_5_out));  // open: en
  and and_1 (and_1_out, decoder_1_out6, comparator_1_eq);
  full_8_bit_alu full_8_bit_alu_1 (
    .cin(or_3_out), .in_2(out_17), .in_3(out_18), .Bin(xor_1_out), .opcode(out_21), .out_6(out_12),
    .out_7(out_19), .out_8(out_22));
  Comparator comparator_1 (.a(out_22), .b({8{1'b1}}), .eq(comparator_1_eq));  // open: gt, lt
  or or_5 (or_5_out, decoder_1_out7, and_1_out);
  RAM #(.bus("separate")) ram_1 (
    .addr(out_12), .din(out_16), .data(ram_1_data), .str(decoder_1_out4), .clk(clock_1_out),
    .ld(decoder_1_out3), .clr(CLR));  // open: sel
  Hex_Digit_Display hex_digit_display_1 (.value(out_7[7:4]));  // open: dp
  Multiplexer #(.width(8)) multiplexer_8 (.in0(ram_1_data), .in1(out_12), .out(out_8), .sel(or_6_out));  // open: en
  Hex_Digit_Display hex_digit_display_2 (.value(out_7[3:0]));  // open: dp
  Multiplexer #(.width(8)) multiplexer_9 (.in1(out_17), .out(out_7), .sel(decoder_1_out13));  // open: in0, en
  or or_6 (or_6_out, decoder_1_out2, decoder_1_out10, decoder_1_out11, decoder_1_out0, decoder_1_out1, decoder_1_out5, decoder_1_out8, decoder_1_out12, decoder_1_out13, decoder_1_out14, decoder_1_out15);

  assign out_14 = out_2;
  assign out_20 = out_8;
  assign out_23 = out_16;

  // Notes on the sheet:
  //   Clk
  //   Clr 1
  //   Bin
  //   Clr 2
  //   contents of rom_1 (hex, n*v repeats v):
  //   ec b2 2f 1d 6f 2f 1e 27 d4 4*14 16 d4
endmodule
